// Digital circuit state_char.dig as structural Verilog
module state_char (
  input  [7:0] D,
  output next,
  output done,
  output send,
  output fill
);

  wire comparator_1_eq, not_1_out, not_2_out, not_3_out;

  Comparator #(.Bits(8)) comparator_1 (.a(D), .b({8{1'b0}}), .eq(comparator_1_eq));  // open: gt, lt
  not not_1 (not_1_out, comparator_1_eq);
  not not_2 (not_2_out, D[0]);
  and and_1 (next, not_2_out, D[3], D[1]);
  and and_2 (done, not_2_out, D[3], D[2]);
  and and_3 (send, not_2_out, D[3], D[4]);
  not not_3 (not_3_out, D[3]);
  and and_4 (fill, not_2_out, not_1_out, not_3_out);
endmodule
